# Fritzing sketch fritzing (saved by Fritzing 1.0.4)
breadboards: 2

parts:
  Thermal_imaging_camera = Adafruit MLX90640 Thermal Camera [part_number="Adafruit #4407"]
  Arduino_MKR_WiFi_1010 = hi
  SCD30_(CO₂_Temperature_and_Humidity) = Adafruit SCD30 [part_number="Adafruit #4867"]
  TFT_eSPI_Display = Adafruit 3.5 inch 480x320 Capacitive Touch Display [part_number=#5846]
  Q1 = MOSFET-NCHANNEL [package=to220v]
  Fan = DC Motor [voltage_(max)=6V voltage_(min)=3V]
  Curtain = Basic Servo
  VCC1 = Battery [internal_resistance=0.1Ω]
  Light_Sensor = Ambient Light Sensor (TEMT6000 Breakout Board)

nets:
  VCC: Thermal_imaging_camera.VCC, Arduino_MKR_WiFi_1010.VCC, TFT_eSPI_Display.VCC, Light_Sensor.VCC
  N1: Thermal_imaging_camera.SCL, Arduino_MKR_WiFi_1010.A5/SCL, SCD30_(CO₂_Temperature_and_Humidity).SCL, TFT_eSPI_Display.CTP_SCL_5V
  GND: Thermal_imaging_camera.GND, Arduino_MKR_WiFi_1010.GND, SCD30_(CO₂_Temperature_and_Humidity).GND, TFT_eSPI_Display.GND, Q1.S, Curtain.gnd, VCC1.-, Light_Sensor.GND
  N2: Thermal_imaging_camera.SDA, Arduino_MKR_WiFi_1010.A4/SDA, SCD30_(CO₂_Temperature_and_Humidity).SDA, TFT_eSPI_Display.CTP_SDA_5V
  N3: Arduino_MKR_WiFi_1010.D6_PWM, Curtain.pulse
  N4: Arduino_MKR_WiFi_1010.D7, Q1.G
  N5: Arduino_MKR_WiFi_1010.D8, TFT_eSPI_Display.SDI_5V
  N6: Arduino_MKR_WiFi_1010.D10_PWM/SS, TFT_eSPI_Display.SDO
  N7: Arduino_MKR_WiFi_1010.DTR_(Reset), TFT_eSPI_Display.LCD_RST_5V
  N8: Arduino_MKR_WiFi_1010.A1, Light_Sensor.S
  N9: Q1.D, Fan.pin_2
  N10: Fan.pin_1, Curtain.vcc, VCC1.+

custom parts:
  Adafruit MLX90640 Thermal Camera: You can now add affordable heat-vision to your project and with an Adafruit MLX90640 Thermal Camera Breakout. This sensor contains a 24x32 array of IR thermal sensors. When connected to your microcontroller (or Raspberry Pi) it will return an array of 768 individual infrared temperature readings over I2C. It's like those fancy thermal cameras, but compact and simple enough for easy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
  hi: The Arduino Funnel I/O (Fio) is a board designed by Shigeru Kobayashi, based on the original design from LilyPad. Funnel is a toolkit to sketch your idea physically, and consists of software libraries and hardware. By using Funnel, the user can interface to sensors and/or actuators with various programming languages such as ActionScript 3, Processing, and Ruby. Arduino Fio is compatible with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
  Adafruit 3.5 inch 480x320 Capacitive Touch Display: Add some jazz & pizazz to your project with a color touchscreen LCD. This TFT display is big (3.5" diagonal) bright (6 white-LED backlight) and colorful! 480x320 pixels with individual RGB pixel control, this has way more resolution than a black and white 128x64 display, and double our 2.8" TFT. As a bonus, this display has a capacitive touchscreen attached to it already, so you can detect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
